// Logisim project lights_off_project.circ as structural Verilog: 1 circuit, main circuit main
module main (
);

  wire button_1_out, button_2_out, button_3_out, button_4_out, button_5_out, button_6_out, button_7_out,
       button_8_out, or_4_out;
  wire [3:0] or_3_out, register_1_q;
  wire [8:0] register_2_q, rom_1_data, xor_1_out;

  or or_1 (or_3_out[2], button_8_out, button_4_out, button_6_out, button_5_out);
  Button button_1 (.out(button_1_out));
  Button button_2 (.out(button_2_out));
  Button button_3 (.out(button_3_out));
  Button button_4 (.out(button_4_out));
  Button button_5 (.out(button_5_out));
  Button button_6 (.out(button_6_out));
  Register #(.width(4)) register_1 (.D(or_3_out), .clk(or_4_out), .Q(register_1_q));  // open: en, clr
  or or_2 (or_3_out[1], button_6_out, button_3_out, button_5_out, button_7_out);
  Button button_7 (.out(button_7_out));
  Button button_8 (.out(button_8_out));
  Button button_9 (.out(or_3_out[3]));
  LED led_1 (.in(register_2_q[0]));
  LED led_2 (.in(register_2_q[1]));
  LED led_3 (.in(register_2_q[2]));
  LED led_4 (.in(register_2_q[3]));
  LED led_5 (.in(register_2_q[4]));
  LED led_6 (.in(register_2_q[6]));
  LED led_7 (.in(register_2_q[7]));
  LED led_8 (.in(register_2_q[8]));
  or or_3 (or_3_out[0], button_6_out, button_8_out, button_3_out, button_2_out);
  LED led_9 (.in(register_2_q[5]));
  ROM #(.addrWidth(4), .dataWidth(9)) rom_1 (.addr(register_1_q), .data(rom_1_data));
  or or_4 (or_4_out, button_2_out, button_7_out, button_3_out, button_5_out, button_6_out, button_4_out, button_8_out, or_3_out[3], button_1_out);
  Register #(.trigger("falling"), .width(9)) register_2 (
    .D(xor_1_out), .clk(or_4_out), .Q(register_2_q));  // open: en, clr
  assign xor_1_out = rom_1_data ^ register_2_q;  // XOR_Gate xor_1, 9 bits wide

  // Notes on the sheet:
  //   contents of rom_1 (hex, n*v repeats v):
  //   b 17 26 59 ba 134 c8 1d0 1a0
endmodule
