// Logisim project lights_out_3.circ as structural Verilog: 1 circuit, main circuit main
module main (
);

  wire btn0, btn1, btn2, btn3, btn4, btn5, btn6, btn7, btn8, light0, light1, light2, light3, light4, light5,
       light6, light7, light8, or_1_out, sigAnyPress, sigReset, sigWin;
  wire [2:0] sigAddr;
  wire [7:0] sigMoves;
  wire [8:0] multiplexer_1_out, sigMask, sigPreset, xor_1_out;

  Button button_1 (.out(sigReset));
  Hex_Digit_Display #(.decimalPoint("false")) hex_digit_display_1 (.value(sigMoves[3:0]));
  LED led_1 (.in(sigWin));
  Hex_Digit_Display #(.decimalPoint("false")) hex_digit_display_2 (.value(sigMoves[7:4]));
  LED led_2 (.in(light0));
  Button button_2 (.out(btn8));
  Button button_3 (.out(btn5));
  Button button_4 (.out(btn2));
  assign xor_1_out = sigMask ^ {light0, light1, light2, light3, light4, light5, light6, light7, light8};  // XOR_Gate xor_1, 9 bits wide
  Button button_5 (.out(btn7));
  LED led_3 (.in(light3));
  LED led_4 (.in(light6));
  Multiplexer #(.width(9)) multiplexer_1 (.in0(xor_1_out), .in1(sigPreset), .out(multiplexer_1_out), .sel(sigReset));
  LED led_5 (.in(light1));
  Button button_6 (.out(btn4));
  LED led_6 (.in(light4));
  Button button_7 (.out(btn1));
  LED led_7 (.in(light7));
  or or_1 (or_1_out, sigAnyPress, sigReset);
  Button button_8 (.out(btn6));
  LED led_8 (.in(light2));
  Button button_9 (.out(btn3));
  Button button_10 (.out(btn0));
  Register #(.trigger("falling"), .width(9)) register_1 (
    .D(multiplexer_1_out), .clk(or_1_out),
    .Q({light0, light1, light2, light3, light4, light5, light6, light7, light8}));  // open: en, clr
  LED led_9 (.in(light5));
  LED led_10 (.in(light8));
  or or_2 (sigAddr[0], btn1, btn3, btn5, btn7);
  or or_3 (sigAddr[1], btn2, btn3, btn6, btn7);
  or or_4 (sigAddr[2], btn4, btn5, btn6, btn7);
  or or_5 (sigAnyPress, btn0, btn1, btn2, btn3, btn4, btn5, btn6, btn7, btn8);
  Random #(.width(9)) random_1 (.next(1'b1), .clk(sigReset), .out(sigPreset));  // open: clr
  ROM #(.addrWidth(4), .dataWidth(9)) rom_1 (.addr({btn8, sigAddr}), .data(sigMask));
  nor nor_1 (sigWin, light0, light1, light2, light3, light4, light5, light6, light7, light8);
  Counter counter_1 (.clr(sigReset), .clk(sigAnyPress), .Q(sigMoves));  // open: load, up, count, D, carry

  // Other names for the same wires on the sheet: sigAddr[3] = btn8;
  //   sigState[8:0] = {light0, light1, light2, light3, light4, light5, light6, light7, light8}

  // Notes on the sheet:
  //   MOVE COUNTER
  //   === GAME CONTROLS ===
  //   Hit Reset for New Random Board
  //   VICTORY STATUS
  //   LIGHTS OUT - 3x3 PUZZLE GAME
  //   Select Poke Tool (Finger) -> Click any Light Button in the 3x3 Grid below! Goal: Turn ALL lights OFF.
  //   === STATE REGISTER & TOGGLE ENGINE ===
  //   === BUTTON ENCODER (9 to 4) ===
  //   contents of rom_1 (hex, n*v repeats v):
  //   b 17 26 59 ba 134 c8 1d0 1a0
  //   === WIN DETECTOR ===
  //   === RANDOM STATE GENERATOR ===
  //   === BITMASK ROM (16x9) ===
  //   === MOVE COUNTER ENGINE ===
endmodule
