// Logisim project lights_out_4x4.circ as structural Verilog: 1 circuit, main circuit main
module main (
);

  wire btn0, btn1, btn2, btn3, btn4, btn5, btn6, btn7, btn8, btn9, btn10, btn11, btn12, btn13, btn14, btn15,
       light0, light1, light2, light3, light4, light5, light6, light7, light8, light9, light10, light11,
       light12, light13, light14, light15, or_1_out, sigAnyPress, sigReset, sigWin;
  wire [3:0] sigAddr;
  wire [7:0] sigMoves;
  wire [15:0] multiplexer_1_out, sigMask, sigPreset, xor_1_out;

  Button button_1 (.out(sigReset));
  LED led_1 (.in(sigWin));
  Hex_Digit_Display #(.decimalPoint("false")) hex_digit_display_1 (.value(sigMoves[3:0]));
  Hex_Digit_Display #(.decimalPoint("false")) hex_digit_display_2 (.value(sigMoves[7:4]));
  assign xor_1_out = sigMask ^ {light15, light14, light13, light12, light11, light10, light9, light8, light7, light6, light5, light4, light3, light2, light1, light0};  // XOR_Gate xor_1, 16 bits wide
  LED led_2 (.in(light0));
  LED led_3 (.in(light4));
  Button button_2 (.out(btn8));
  LED led_4 (.in(light8));
  Button button_3 (.out(btn12));
  LED led_5 (.in(light12));
  Multiplexer #(.width(16)) multiplexer_1 (.in0(xor_1_out), .in1(sigPreset), .out(multiplexer_1_out), .sel(sigReset));
  Button button_4 (.out(btn0));
  Button button_5 (.out(btn4));
  Button button_6 (.out(btn9));
  Button button_7 (.out(btn13));
  Register #(.trigger("falling"), .width(16)) register_1 (
    .D(multiplexer_1_out), .clk(or_1_out),
    .Q({light15, light14, light13, light12, light11, light10, light9, light8, light7, light6, light5, light4, light3, light2, light1, light0}));  // open: en, clr
  or or_1 (or_1_out, sigAnyPress, sigReset);
  LED led_6 (.in(light1));
  Button button_8 (.out(btn1));
  LED led_7 (.in(light2));
  LED led_8 (.in(light5));
  Button button_9 (.out(btn5));
  LED led_9 (.in(light6));
  LED led_10 (.in(light9));
  Button button_10 (.out(btn10));
  LED led_11 (.in(light13));
  Button button_11 (.out(btn14));
  Button button_12 (.out(btn2));
  Button button_13 (.out(btn6));
  LED led_12 (.in(light10));
  Button button_14 (.out(btn11));
  LED led_13 (.in(light14));
  Button button_15 (.out(btn15));
  LED led_14 (.in(light3));
  Button button_16 (.out(btn3));
  LED led_15 (.in(light7));
  Button button_17 (.out(btn7));
  LED led_16 (.in(light11));
  LED led_17 (.in(light15));
  or or_2 (sigAnyPress, btn0, btn1, btn2, btn3, btn4, btn5, btn6, btn7, btn8, btn9, btn10, btn11, btn12, btn13, btn14, btn15);
  or or_3 (sigAddr[0], btn1, btn3, btn5, btn7, btn9, btn11, btn13, btn15);
  or or_4 (sigAddr[1], btn2, btn3, btn6, btn7, btn10, btn11, btn14, btn15);
  or or_5 (sigAddr[2], btn4, btn5, btn6, btn7, btn12, btn13, btn14, btn15);
  or or_6 (sigAddr[3], btn8, btn9, btn10, btn11, btn12, btn13, btn14, btn15);
  nor nor_1 (sigWin, light0, light1, light2, light3, light4, light5, light6, light7, light8, light9, light10, light11, light12, light13, light14, light15);
  ROM #(.addrWidth(4), .dataWidth(16)) rom_1 (.addr(sigAddr), .data(sigMask));
  Counter counter_1 (.clr(sigReset), .clk(sigAnyPress), .Q(sigMoves));  // open: load, up, count, D, carry
  Random #(.width(16)) random_1 (.next(1'b1), .clk(sigReset), .out(sigPreset));  // open: clr

  // Other names for the same wires on the sheet: sigState[15:0] = {light15, light14, light13, light12, light11, light10, light9, light8, light7, light6, light5, light4, light3, light2, light1, light0}

  // Notes on the sheet:
  //   GAME CONTROLS
  //   RESET GAME
  //   MOVE COUNTER
  //   VICTORY STATUS
  //   STATE REGISTER
  //   LIGHTS OUT - 4x4 HARDWARE PUZZLE GAME
  //   Select Poke Tool (Finger) -> Click any Button in the 4x4 Grid to toggle it & its neighbors.
  //   Goal: Turn ALL 16 lights OFF to WIN!
  //   BUTTON ENCODER (16 to 4 bit)
  //   WIN DETECTOR (1 if All lights are off)
  //   contents of rom_1 (hex, n*v repeats v):
  //   13 27 4e 8c 131 272 4e4 8c8 1310 2720 4e40 8c80 3100 7200 e400 c800
  //   BITMASK ROM (Consists of preset of each button)
  //    MOVE COUNTER ENGINE 
  //   RANDOM STATE GENERATOR
endmodule
